// Logisim project circuito.circ as structural Verilog
module arreglo_8bits (
  input  [7:0] numero_entrada,
  input  reset,
  input  reloj,
  output [7:0] numero_salida
);

  wire j_k_ff_1_qn, j_k_ff_2_qn, j_k_ff_3_qn, j_k_ff_4_qn, j_k_ff_5_qn, j_k_ff_6_qn, j_k_ff_7_qn, j_k_ff_8_qn;

  J_K_Flip_Flop j_k_ff_1 (
    .J(numero_entrada[7]), .K(j_k_ff_1_qn), .clk(reloj), .Q(numero_salida[7]), .Qn(j_k_ff_1_qn), .reset(reset));  // open: preset
  J_K_Flip_Flop j_k_ff_2 (
    .J(numero_entrada[6]), .K(j_k_ff_2_qn), .clk(reloj), .Q(numero_salida[6]), .Qn(j_k_ff_2_qn), .reset(reset));  // open: preset
  J_K_Flip_Flop j_k_ff_3 (
    .J(numero_entrada[5]), .K(j_k_ff_3_qn), .clk(reloj), .Q(numero_salida[5]), .Qn(j_k_ff_3_qn), .reset(reset));  // open: preset
  J_K_Flip_Flop j_k_ff_4 (
    .J(numero_entrada[4]), .K(j_k_ff_4_qn), .clk(reloj), .Q(numero_salida[4]), .Qn(j_k_ff_4_qn), .reset(reset));  // open: preset
  J_K_Flip_Flop j_k_ff_5 (
    .J(numero_entrada[3]), .K(j_k_ff_5_qn), .clk(reloj), .Q(numero_salida[3]), .Qn(j_k_ff_5_qn), .reset(reset));  // open: preset
  J_K_Flip_Flop j_k_ff_6 (
    .J(numero_entrada[2]), .K(j_k_ff_6_qn), .clk(reloj), .Q(numero_salida[2]), .Qn(j_k_ff_6_qn), .reset(reset));  // open: preset
  J_K_Flip_Flop j_k_ff_7 (
    .J(numero_entrada[1]), .K(j_k_ff_7_qn), .clk(reloj), .Q(numero_salida[1]), .Qn(j_k_ff_7_qn), .reset(reset));  // open: preset
  J_K_Flip_Flop j_k_ff_8 (
    .J(numero_entrada[0]), .K(j_k_ff_8_qn), .clk(reloj), .Q(numero_salida[0]), .Qn(j_k_ff_8_qn), .reset(reset));  // open: preset
endmodule

module vector (
  input  [7:0] numero_entrada,
  input  [3:0] posicion,
  input  reset,
  input  reloj,
  output [7:0] numero_salida
);

  wire [7:0] demultiplexer_1_out0, demultiplexer_1_out1, demultiplexer_1_out2, demultiplexer_1_out3,
       demultiplexer_1_out4, demultiplexer_1_out5, demultiplexer_1_out6, demultiplexer_1_out7,
       demultiplexer_1_out8, demultiplexer_1_out9, demultiplexer_1_out10, demultiplexer_1_out11,
       demultiplexer_1_out12, demultiplexer_1_out13, demultiplexer_1_out14, demultiplexer_1_out15,
       position_0_numero_salida, position_1_numero_salida, position_2_numero_salida,
       position_3_numero_salida, position_4_numero_salida, position_5_numero_salida,
       position_6_numero_salida, position_7_numero_salida, position_8_numero_salida,
       position_9_numero_salida, position_10_numero_salida, position_11_numero_salida,
       position_12_numero_salida, position_13_numero_salida, position_14_numero_salida,
       position_15_numero_salida;

  Demultiplexer #(.select(4), .width(8)) demultiplexer_1 (
    .out0(demultiplexer_1_out0), .out1(demultiplexer_1_out1), .out2(demultiplexer_1_out2),
    .out3(demultiplexer_1_out3), .out4(demultiplexer_1_out4), .out5(demultiplexer_1_out5),
    .out6(demultiplexer_1_out6), .out7(demultiplexer_1_out7), .out8(demultiplexer_1_out8),
    .out9(demultiplexer_1_out9), .out10(demultiplexer_1_out10), .out11(demultiplexer_1_out11),
    .out12(demultiplexer_1_out12), .out13(demultiplexer_1_out13), .out14(demultiplexer_1_out14),
    .out15(demultiplexer_1_out15), .in(numero_entrada), .sel(posicion));
  arreglo_8bits position_0 (
    .numero_entrada(demultiplexer_1_out0), .reset(reset), .reloj(reloj),
    .numero_salida(position_0_numero_salida));
  arreglo_8bits position_1 (
    .numero_entrada(demultiplexer_1_out1), .reset(reset), .reloj(reloj),
    .numero_salida(position_1_numero_salida));
  arreglo_8bits position_2 (
    .numero_entrada(demultiplexer_1_out2), .reset(reset), .reloj(reloj),
    .numero_salida(position_2_numero_salida));
  arreglo_8bits position_3 (
    .numero_entrada(demultiplexer_1_out3), .reset(reset), .reloj(reloj),
    .numero_salida(position_3_numero_salida));
  arreglo_8bits position_4 (
    .numero_entrada(demultiplexer_1_out4), .reset(reset), .reloj(reloj),
    .numero_salida(position_4_numero_salida));
  arreglo_8bits position_5 (
    .numero_entrada(demultiplexer_1_out5), .reset(reset), .reloj(reloj),
    .numero_salida(position_5_numero_salida));
  arreglo_8bits position_6 (
    .numero_entrada(demultiplexer_1_out6), .reset(reset), .reloj(reloj),
    .numero_salida(position_6_numero_salida));
  arreglo_8bits position_7 (
    .numero_entrada(demultiplexer_1_out7), .reset(reset), .reloj(reloj),
    .numero_salida(position_7_numero_salida));
  arreglo_8bits position_8 (
    .numero_entrada(demultiplexer_1_out8), .reset(reset), .reloj(reloj),
    .numero_salida(position_8_numero_salida));
  arreglo_8bits position_9 (
    .numero_entrada(demultiplexer_1_out9), .reset(reset), .reloj(reloj),
    .numero_salida(position_9_numero_salida));
  arreglo_8bits position_10 (
    .numero_entrada(demultiplexer_1_out10), .reset(reset), .reloj(reloj),
    .numero_salida(position_10_numero_salida));
  arreglo_8bits position_11 (
    .numero_entrada(demultiplexer_1_out11), .reset(reset), .reloj(reloj),
    .numero_salida(position_11_numero_salida));
  arreglo_8bits position_12 (
    .numero_entrada(demultiplexer_1_out12), .reset(reset), .reloj(reloj),
    .numero_salida(position_12_numero_salida));
  arreglo_8bits position_13 (
    .numero_entrada(demultiplexer_1_out13), .reset(reset), .reloj(reloj),
    .numero_salida(position_13_numero_salida));
  arreglo_8bits position_14 (
    .numero_entrada(demultiplexer_1_out14), .reset(reset), .reloj(reloj),
    .numero_salida(position_14_numero_salida));
  arreglo_8bits position_15 (
    .numero_entrada(demultiplexer_1_out15), .reset(reset), .reloj(reloj),
    .numero_salida(position_15_numero_salida));
  Multiplexer #(.select(4), .width(8)) multiplexer_1 (
    .in0(position_0_numero_salida), .in1(position_1_numero_salida), .in2(position_2_numero_salida),
    .in3(position_3_numero_salida), .in4(position_4_numero_salida), .in5(position_5_numero_salida),
    .in6(position_6_numero_salida), .in7(position_7_numero_salida), .in8(position_8_numero_salida),
    .in9(position_9_numero_salida), .in10(position_10_numero_salida), .in11(position_11_numero_salida),
    .in12(position_12_numero_salida), .in13(position_13_numero_salida), .in14(position_14_numero_salida),
    .in15(position_15_numero_salida), .out(numero_salida), .sel(posicion));
endmodule
